# Fritzing sketch Eksempel2_IO (saved by Fritzing 0.9.3b)
breadboards: 1

parts:
  Part1 = Arduino Uno (Rev3)
  LED1 = LED - 5mm [color="Red (633nm)" package="5 mm [THT]"]
  R1 = Resistor [tolerance=±5% resistance=220 power=5W package=THT]
  R2 = Resistor [tolerance=±5% resistance=10k package=THT]
  S1 = Pushbutton [package="[THT]"]

nets:
  N1: Part1.D12/MISO, R2.Pin_1, S1.Pin_1, S1.Pin_2
  N2: Part1.D13/SCK, R1.Pin_0
  N3: Part1.GND, LED1.cathode, R2.Pin_0
  N4: Part1.5V, S1.Pin_3, S1.Pin_4
  N5: LED1.anode, R1.Pin_1

// code stored in the sketch: Eksempel2_IO.ino
const int ledPin = 13; // ledPin sættes op til at holde "adressen" på pin 13.
const int buttonPin = 12; // buttonPin sættes op til at holde "adressen" på pin 12.

// Boolske værdier er enten sande eller falske.
bool ledState = false; // En variabel ledState initialiseres som en Boolsk false.

void setup() {
  pinMode(ledPin, OUTPUT); // LED'ens I/O pin sættes op som output.
  pinMode(buttonPin, INPUT); // Knappens'ens I/O pin sættes op som input.
}

void loop() {
  if (digitalRead(buttonPin) == HIGH){ // Hvis buttonPin er lig med Høj/1/sand/tændt:
    
    // !-Operatoren bruges til at få det omvendte.
    ledState = !ledState; // Så ledState skifter til den modsatte værdi.
    digitalWrite(ledPin, ledState); //Så sættes ledPin til ledStates værdi.
    
    //delay()-funktionen venter i det antal millisekunder, den modtager.
    delay(200); // Der ventes 200 millisekunder for at undgå mekanisk prel.
  }
}
