# Fritzing sketch Eksempel1_DC_Motor_Driver (saved by Fritzing 0.9.3b)
breadboards: 1

parts:
  Part1 = Arduino Uno (Rev3)
  Q1 = NPN-Transistor [package="TO92 [THT]"]
  R1 = Resistor [tolerance=±5% resistance=220 package=THT]
  M1 = DC Motor
  U1 = POT [package=pot_mammoth]

nets:
  N1: Part1.A0, U1.A
  N2: Part1.D5_PWM, R1.Pin_1
  N3: Part1.5V, M1.pin_1, U1.S
  N4: Part1.GND, Q1.E, U1.E
  N5: Q1.B, R1.Pin_0
  N6: Q1.C, M1.pin_2

// code stored in the sketch: Eksempel1_DC_Motor_Driver.ino
#define MOTORPIN 9
#define AIN A0

int potRead = 0;
int motorSpeed = 0;

void setup(){
	pinMode(MOTORPIN, OUTPUT);
	Serial.begin(9600);
}

void loop(){
	potRead = analogRead(AIN);
	motorSpeed = potRead/4;
	analogWrite(MOTORPIN, motorSpeed);
	Serial.print("potRead = "); Serial.println(potRead); // potReads værdi skrives ud på den serielle forbindelse.
  Serial.print("motorSpeed = "); Serial.println(motorSpeed); // servoPos' værdi skrives ud på den serielle forbindelse.
}
