# Fritzing sketch Eksempel2_Servo_Driving (saved by Fritzing 0.9.3b)
breadboards: 1

parts:
  Part1 = Arduino Uno (Rev3)
  M1 = Dagu DGServo 9g (Top view) [part_number=RS001B]
  U1 = POT [package=pot_mammoth]

nets:
  N1: Part1.A0, U1.A
  N2: Part1.D9_PWM, M1.pulse
  5V: Part1.5V, M1.vcc, U1.S
  GND: Part1.GND, M1.gnd, U1.E

// code stored in the sketch: Eksempel2_Servo_Driving.ino
#include <Servo.h> // Her inkluderes Servo biblioteket.

#define SERVPIN 9 // Servopinnen defineres til at være pin 9
#define AIN A0 // Pinnen til analog læsning bliver defineret.

Servo myServo; // Et servo-objekt, myServo instantieres.
int potRead = 0; // potRead initialiseres til 0.
int servoPos = 0; // Servopositionen servoPos instantieres til 0.

long unsigned timer = 0;

void setup() {
  myServo.attach(SERVPIN); // myServo sættes til på pin 9 (PWM pin).
  Serial.begin(9600); // Den serielle forbindelse påbegyndes.
}

void loop() {
  potRead = analogRead(AIN); // potentiometret aflæses til potRead.
  servoPos = map(potRead, 0, 1023, 1, 179); // potRead omregnes til en servoPos.
  myServo.write(servoPos); // servoPos (i grader) skrives til myServo.

  if(timer <= millis() - 1000){
    Serial.print("potRead = "); Serial.println(potRead); // potReads værdi skrives ud på den serielle forbindelse.
    Serial.print("servoPos = "); Serial.println(servoPos); // servoPos' værdi skrives ud på den serielle forbindelse.
    timer = millis();
  }
  
}
