# Fritzing sketch Eksempel5_7-Segment_Display (saved by Fritzing 0.9.3b)
breadboards: 1

parts:
  Part1 = Arduino Uno (Rev3)
  DI1 = 7-Segment LED Display [package=THT]
  R1 = Resistor [tolerance=±5% resistance=220 package=THT]
  R2 = Resistor [tolerance=±5% resistance=220 package=THT]
  R3 = Resistor [tolerance=±5% resistance=220 package=THT]
  R4 = Resistor [tolerance=±5% resistance=220 package=THT]
  R5 = Resistor [tolerance=±5% resistance=220 package=THT]
  R6 = Resistor [tolerance=±5% resistance=220 package=THT]
  R7 = Resistor [tolerance=±5% resistance=220 package=THT]
  R8 = Resistor [tolerance=±5% resistance=220 package=THT]
  U1 = 74HC595 [package="DIP16 [THT]"]

nets:
  N1: Part1.D5_PWM, U1.DS
  N2: Part1.D6_PWM, U1.ST_CP
  N3: Part1.D7, U1.SH_CP
  5V: Part1.5V, U1.MR, U1.VCC
  GND: Part1.GND, DI1.commAnode, U1.GND, U1.OE
  N4: DI1.cathodeE, R7.Pin_0
  N5: DI1.cathodeD, R8.Pin_0
  N6: DI1.cathodeC, R5.Pin_1
  N7: DI1.cathodeDP, R6.Pin_1
  N8: DI1.cathodeB, R1.Pin_1
  N9: DI1.cathodeA, R3.Pin_1
  N10: DI1.cathodeF, R2.Pin_0
  N11: DI1.cathodeG, R4.Pin_0
  N12: R1.Pin_0, U1.Q1
  N13: R2.Pin_1, U1.Q5
  N14: R4.Pin_1, U1.Q6
  N15: R5.Pin_0, U1.Q2
  N16: R6.Pin_0, U1.Q7
  N17: R7.Pin_1, U1.Q4
  N18: R8.Pin_1, U1.Q3

// code stored in the sketch: Eksempel5_7-Segment_Display.ino
#define CLOCKPIN 7
#define LATCHPIN 6
#define DATAPIN 5

#define BTNPIN 4

int count = 0;
long int wait = 0;

/*
int ssegArray[10] = {B11111100,
                    B01100000,
                    B11011010,
                    B11110010,
                    B01100110,
                    B10110110,
                    B10111110,
                    B11100000,
                    B11111110,
                    B11100110};
*/

int ssegArray[10] = {252,
                    96,
                    218,
                    242,
                    102,
                    182,
                    190,
                    224,
                    254,
                    230};

void setup() {
  pinMode(BTNPIN, INPUT);
  pinMode(CLOCKPIN, OUTPUT);
  pinMode(LATCHPIN, OUTPUT);
  pinMode(DATAPIN, OUTPUT);
  wait = millis();
  digitalWrite(LATCHPIN, LOW);
  shiftOut(DATAPIN, CLOCKPIN, LSBFIRST, ssegArray[count]);
  digitalWrite(LATCHPIN, HIGH);
}

void loop() {
  if((digitalRead(BTNPIN) == HIGH) && (millis() >= wait+200)){
    wait = millis();
    count++;
    if(count >= 10){
      count = 0;
    }
    digitalWrite(LATCHPIN, LOW);
    shiftOut(DATAPIN, CLOCKPIN, LSBFIRST, ssegArray[count]);
    digitalWrite(LATCHPIN, HIGH);
  }
}
