# Fritzing sketch Eksempel2_L293D_Motorstyring (saved by Fritzing 0.9.3b)
breadboards: 1

parts:
  Part1 = Arduino Uno (Rev3)
  IC1 = L293D [package=THT]
  M1 = DC Motor
  R1 = Resistor [tolerance=±5% resistance=10k package=THT]
  S1 = Pushbutton [package="[THT]"]
  U1 = POT [package=pot_alpha_rv16af-20]
  VCC1 = Battery block 9V

nets:
  N1: Part1.A0, U1.S
  N2: Part1.D8, R1.Pin_1, S1.Pin_1, S1.Pin_2
  N3: Part1.D3_PWM, IC1.In_2
  N4: Part1.D4, IC1.In_1
  N5: Part1.D5_PWM, IC1.Enable_1
  N6: Part1.5V, IC1.+V, S1.Pin_3, S1.Pin_4, U1.A
  N7: Part1.GND, IC1.0V, R1.Pin_0, U1.E, VCC1.-
  N8: IC1.Out_1_(_Controlled_by_Enable_1_), M1.pin_1
  N9: IC1.Out_2_(_Controlled_by_Enable_1_), M1.pin_2
  N10: IC1.+Vmotor, VCC1.+

// code stored in the sketch: Eksempel2_L293D_Motorstyring.ino
#define EN  5 // Enable pin
#define FWD 4 // Pin til det fremadg?ende signal
#define BCK 3 // Pin til det bagudg?ende

#define BTN 8 // Knappens pin
#define AIN // Analog input

#define FORWARD 1
#define BACK 0

boolean direction = 1;
int speed = 0;
int turnMotor (boolean dir, int spd); // Vores egen funktion deklareres.

unsigned long timer = 0;

void setup() {
	// BTN er input.
	pinMode(BTN, INPUT);
	
  // Alle pins sættes til output:
  pinMode(FWD, OUTPUT);
  pinMode(BCK, OUTPUT);
  pinMode(EN, OUTPUT);

	// Set timer:
	timer = millis();
}

void loop() {

	if(digitalRead(BTN) == HIGH && (millis() > timer + 200)){
		direction = !direction;
	}

	speed = analogRead(AIN)/4;
	
	turnMotor(direction,speed);

}


// Definitionen p? vores egen funktion:
int turnMotor (boolean dir, int spd){ // Tager to argumenter: dit og spd.
  switch (dir){ // Afhængig af retning, sættes FWD og BCK forskelligt.
    case FORWARD:
      digitalWrite(BCK, LOW);
      digitalWrite(FWD, HIGH);
      analogWrite(EN, spd);
      break;
    case BACK:
      digitalWrite(FWD, LOW);
      digitalWrite(BCK, HIGH);
      analogWrite(EN, spd);
      break;
    default:
      digitalWrite(FWD, LOW);
      digitalWrite(BCK, LOW);
      analogWrite(EN, 0);
      return -1;
      break;
  }
  return 0;
}

// code stored in the sketch: Eksempel4_L293D_Motorstyring.ino
#define EN  5 // Enable pin
#define FWD 4 // Pin til det fremadgående signal
#define BCK 3 // Pin til det bagudgående

enum direction {FORWARD, BACK}; // En enumerering af to tilstande, frem og tilbage.
int turnMotor (direction dir, int spd); // Vores egen funktion deklareres.

void setup() {
  // Alle pins sættes til output:
  pinMode(FWD, OUTPUT);
  pinMode(BCK, OUTPUT);
  pinMode(EN, OUTPUT);
}

void loop() {
  // For en mængde tid kører motorerne frem, med trinvis acceleration.
  for (float i = 0; i <= 255; i += 255/5){
    turnMotor(FORWARD, (int)i);
    delay(1000);
  }
  // Og så vender de igen.
  for (float i = 0; i <= 255; i += 255/5){
    turnMotor(BACK, (int)i);
    delay(1000);
  }
}


// Definitionen på vores egen funktion:
int turnMotor (direction dir, int spd){ // Tager to argumenter: dit og spd.
  switch (dir){ // Afhængig af retning, sættes FWD og BCK forskelligt.
    case FORWARD:
      digitalWrite(BCK, LOW);
      digitalWrite(FWD, HIGH);
      analogWrite(EN, spd);
      break;
    case BACK:
      digitalWrite(FWD, LOW);
      digitalWrite(BCK, HIGH);
      analogWrite(EN, spd);
      break;
    default:
      digitalWrite(FWD, LOW);
      digitalWrite(BCK, LOW);
      analogWrite(EN, 0);
      return -1;
      break;
  }
  return 0;
}
