# Fritzing sketch Eksempel4_HC_05_setup (saved by Fritzing 0.9.3b)
breadboards: 1

parts:
  Part1 = Arduino Uno (Rev3)
  Part2 = Bluetooth HC-05 Macho

nets:
  N1: Part1.D9_PWM, Part2.Key
  N2: Part1.D10_PWM/SS, Part2.TXD
  N3: Part1.D11_PWM/MOSI, Part2.RXD
  5V: Part1.5V, Part2.VCC
  GND: Part1.GND, Part2.GND

// code stored in the sketch: Eksempel2_HC_05_setup.ino
#include <SoftwareSerial.h>

#define EN 9 // EN bruges til at sætte HC-05 i AT mode.

SoftwareSerial HC05(10,11); // HC05 pins - RX pin 11, TX pin 10

void setup() {
  
  pinMode(EN, OUTPUT);
  digitalWrite(EN, HIGH);
  Serial.begin(9600); // Start serial kommunikation med computeren.
  Serial.println("Enter AT-Commands:"); // Prompt for AT kommandoer.
  HC05.begin(38400); // Sætter HC05 serial hastigheden til 38400 baud. AT mode standardhastighed.

}

void loop() {
  
  // Læser fra HC05 forbindelsen, og skriver det til Arduinos serial.
  if(HC05.available()){
    Serial.write(HC05.read());
  }
  
  // Læser fra Arduino, og sender til HC05:
	// AT-Commands kan findes i en HC-05_AT_commands.pdf
	// Giv modulet et navn med AT+NAME=navn
	// Sæt et nyt kodeord vha. AT+PSWD=kode
	// HUSK at anvende Carriage return OG newline i Serial forbindelsen.
  if(Serial.available()){
    HC05.write(Serial.read());
  }
  
}

// code stored in the sketch: Eksempel4_HC_05_setup.ino
#include <SoftwareSerial.h>

#define EN 9 // EN bruges til at s?tte HC-05 i AT mode.

SoftwareSerial HC05(10,11); // HC05 pins - RX pin 11, TX pin 10

void setup() {
  
  pinMode(EN, OUTPUT);
  digitalWrite(EN, HIGH);
  Serial.begin(9600); // Start serial kommunikation med computeren.
  Serial.println("Enter AT-Commands:"); // Prompt for AT kommandoer.
  HC05.begin(38400); // S?tter HC05 serial hastigheden til 38400 baud. AT mode standardhastighed.

}

void loop() {
  
  // Læser fra HC05 forbindelsen, og skriver det til Arduinos serial.
  if(HC05.available()){
    Serial.write(HC05.read());
  }
  
  // Læser fra Arduino, og sender til HC05:
	// AT-Commands kan findes i en HC-05_AT_commands.pdf
	// Giv modulet et navn med AT+NAME=navn
	// Sæt et nyt kodeord vha. AT+PSWD=kode
	// Sæt baud-rate til 115200 1 stop bit 0 parity, med AT+UART=115200,1,0
	// HUSK at anvende Carriage return OG newline i Serial forbindelsen.
  if(Serial.available()){
    HC05.write(Serial.read());
  }
  
}
