# Fritzing sketch Eksempel4_L293D_Motorstyring (saved by Fritzing 0.9.3b)
breadboards: 1

parts:
  Part1 = Arduino Uno (Rev3)
  IC1 = L293D [package=THT]
  M1 = DC Motor

nets:
  N1: Part1.D3_PWM, IC1.In_2
  N2: Part1.D4, IC1.In_1
  N3: Part1.D5_PWM, IC1.Enable_1
  N4: Part1.5V, IC1.+Vmotor, IC1.+V
  N5: Part1.GND, IC1.0V
  N6: IC1.Out_1_(_Controlled_by_Enable_1_), M1.pin_1
  N7: IC1.Out_2_(_Controlled_by_Enable_1_), M1.pin_2

// code stored in the sketch: Eksempel4_L293D_Motorstyring.ino
#define EN  5 // Enable pin
#define FWD 4 // Pin til det fremadgående signal
#define BCK 3 // Pin til det bagudgående

enum direction {FORWARD, BACK}; // En enumerering af to tilstande, frem og tilbage.
int turnMotor (direction dir, int spd); // Vores egen funktion deklareres.

void setup() {
  // Alle pins sættes til output:
  pinMode(FWD, OUTPUT);
  pinMode(BCK, OUTPUT);
  pinMode(EN, OUTPUT);
}

void loop() {
  // For en mængde tid kører motorerne frem, med trinvis acceleration.
  for (float i = 0; i <= 255; i += 255/5){
    turnMotor(FORWARD, (int)i);
    delay(1000);
  }
  // Og så vender de igen.
  for (float i = 0; i <= 255; i += 255/5){
    turnMotor(BACK, (int)i);
    delay(1000);
  }
}


// Definitionen på vores egen funktion:
int turnMotor (direction dir, int spd){ // Tager to argumenter: dit og spd.
  switch (dir){ // Afhængig af retning, sættes FWD og BCK forskelligt.
    case FORWARD:
      digitalWrite(BCK, LOW);
      digitalWrite(FWD, HIGH);
      analogWrite(EN, spd);
      break;
    case BACK:
      digitalWrite(FWD, LOW);
      digitalWrite(BCK, HIGH);
      analogWrite(EN, spd);
      break;
    default:
      digitalWrite(FWD, LOW);
      digitalWrite(BCK, LOW);
      analogWrite(EN, 0);
      return -1;
      break;
  }
  return 0;
}
