# Fritzing sketch Eksempel5_HC_05_serial (saved by Fritzing 0.9.3b)
breadboards: 1

parts:
  Part1 = Arduino Uno (Rev3)
  Part2 = Bluetooth HC-05 Macho

nets:
  N1: Part1.D10_PWM/SS, Part2.TXD
  N2: Part1.D11_PWM/MOSI, Part2.RXD
  5V: Part1.5V, Part2.VCC
  GND: Part1.GND, Part2.GND

// code stored in the sketch: Eksempel2_HC_05_setup.ino
#include <SoftwareSerial.h>

#define EN 9 // EN bruges til at sætte HC-05 i AT mode.

SoftwareSerial HC05(10,11); // HC05 pins - RX pin 11, TX pin 10

void setup() {
  
  pinMode(EN, OUTPUT);
  digitalWrite(EN, HIGH);
  Serial.begin(9600); // Start serial kommunikation med computeren.
  Serial.println("Enter AT-Commands:"); // Prompt for AT kommandoer.
  HC05.begin(38400); // Sætter HC05 serial hastigheden til 38400 baud. AT mode standardhastighed.

}

void loop() {
  
  // Læser fra HC05 forbindelsen, og skriver det til Arduinos serial.
  if(HC05.available()){
    Serial.write(HC05.read());
  }
  
  // Læser fra Arduino, og sender til HC05:
  if(Serial.available()){
    HC05.write(Serial.read());
  }
  
}

// code stored in the sketch: Eksempel3_HC_05_serial.ino
#include <SoftwareSerial.h>

String data; // String der holder det modtagne data.

SoftwareSerial HC05(10,11); // HC05 pins - RX pin 11, TX pin 10.

void setup()
{
    Serial.begin(9600); // Start serial kommunikation med computeren.
    HC05.begin(115200); // Start serial kommunikation med HC-05 modulet.                              
}
void loop()
{
   if(HC05.available() > 0) // Tjekker om der er data tilgængeligt.
   {
      data = HC05.readStringUntil('#'); // Indlæs en streng fra HC-05 til data, alt der ligger mellem stopkaraktererne '#'.
      Serial.println(data); // Skriv data ud til computeren.        
   }
}

// code stored in the sketch: Eksempel5_HC_05_serial.ino
#include <SoftwareSerial.h>

String data; // String der holder det modtagne data.

SoftwareSerial HC05(10,11); // HC05 pins - RX pin 11, TX pin 10.

void setup()
{
    Serial.begin(9600); // Start serial kommunikation med computeren.
    HC05.begin(115200); // Start serial kommunikation med HC-05 modulet.                              
}
void loop()
{
   if(HC05.available() > 0) // Tjekker om der er data tilgængeligt.
   {
      data = HC05.readStringUntil('#'); // Indlæs en streng fra HC-05 til data, alt der ligger mellem stopkaraktererne '#'.
      Serial.println(data); // Skriv data ud til computeren.        
   }
}
