# Fritzing sketch Eksempel2_Robot_MiniBreadboard (saved by Fritzing 0.9.3b)
breadboards: 1

parts:
  Part3 = Bluetooth HC-05 Macho
  IC2 = L293D [package=THT]
  Part4 = Arduino Uno (Rev3)
  VCC4 = Battery
  VCC5 = Battery
  M3 = DC Motor
  M4 = DC Motor

nets:
  N1: Part3.TXD, Part4.D10_PWM/SS
  N2: Part3.RXD, Part4.D11_PWM/MOSI
  VCC: Part3.VCC, IC2.+V, Part4.5V
  GND: Part3.GND, IC2.0V, Part4.GND, VCC4.-
  N3: IC2.Enable_1, Part4.D5_PWM
  N4: IC2.In_1, Part4.D4
  N5: IC2.Out_1_(_Controlled_by_Enable_1_), M3.pin_2
  N6: IC2.Out_2_(_Controlled_by_Enable_1_), M3.pin_1
  N7: IC2.In_2, Part4.D3_PWM
  N8: IC2.+Vmotor, VCC5.+
  N9: IC2.Enable_2, Part4.D6_PWM
  N10: IC2.In_3, Part4.D8
  N11: IC2.Out_3_(_Controlled_by_Enable_2_), M4.pin_2
  N12: IC2.Out_4_(_Controlled_by_Enable_2_), M4.pin_1
  N13: IC2.In_4, Part4.D7
  N14: VCC4.+, VCC5.-

// code stored in the sketch: Eksempel1_Robot_Breadboard.ino
#include <SoftwareSerial.h> // Include the SoftwareSerial library for serial emulation.

// Left motor's Enable, Forward and Back pins: 
#define L_EN 5
#define L_FWD 4
#define L_BCK 3

// Right motor's Enable, Forward and Back pins:
#define R_EN 6
#define R_FWD 7
#define R_BCK 8

// Virtual RX and TX pins for HC-05 communication:
#define V_RX 10
#define V_TX 11

// Define the legal button inputs:
#define UP "b=1"
#define DOWN "b=2"
#define LEFT "b=3"
#define RIGHT "b=4"

SoftwareSerial HC05(V_RX,V_TX); // Virtual serial connection to the HC-05 Module.

String data; // Datastring for the HC-05 messages.

void setup(){
  motorInitL(); // Initialization function for the left motor.
  motorInitR(); // Initialization function for the right motor.
  HC05.begin(115200); // Initiealizes the communication with HC-05 at 115200 baud.
}

void loop(){

  // Check for new messages from HC-05 module:
  if(HC05.available() > 0){
      data = HC05.readStringUntil('#');
  }

  // If the up button is pressed on joypad:
  if(data.equals(UP)){
    motorSpeedL(255);
    motorSpeedR(255);
  }
  // If the down button is pressed on joypad:
  else if(data.equals(DOWN)){
    motorSpeedL(-255);
    motorSpeedR(-255);
  }
  // If the left button is pressed on joypad:
  else if(data.equals(LEFT)){
    motorSpeedL(0);
    motorSpeedR(255);
  }
  // If the right button is pressed on joypad:
  else if(data.equals(RIGHT)){
    motorSpeedL(255);
    motorSpeedR(0);
  }
  // If no defined button is pressed on joypad:
  else{
    motorSpeedL(0);
    motorSpeedR(0);
  }
}

// code stored in the sketch: Eksempel2_Robot_MiniBreadboard.ino
#include <SoftwareSerial.h> // Include the SoftwareSerial library for serial emulation.

// Left motor's Enable, Forward and Back pins: 
#define L_EN 5
#define L_FWD 4
#define L_BCK 3

// Right motor's Enable, Forward and Back pins:
#define R_EN 6
#define R_FWD 7
#define R_BCK 8

// Virtual RX and TX pins for HC-05 communication:
#define V_RX 10
#define V_TX 11

// Define the legal button inputs:
#define UP "b=1"
#define DOWN "b=2"
#define LEFT "b=3"
#define RIGHT "b=4"

SoftwareSerial HC05(V_RX,V_TX); // Virtual serial connection to the HC-05 Module.

String data; // Datastring for the HC-05 messages.

void setup(){
  motorInitL(); // Initialization function for the left motor.
  motorInitR(); // Initialization function for the right motor.
  HC05.begin(115200); // Initiealizes the communication with HC-05 at 115200 baud.
}

void loop(){

  // Check for new messages from HC-05 module:
  if(HC05.available() > 0){
      data = HC05.readStringUntil('#');
  }

  // If the up button is pressed on joypad:
  if(data.equals(UP)){
    motorSpeedL(255);
    motorSpeedR(255);
  }
  // If the down button is pressed on joypad:
  else if(data.equals(DOWN)){
    motorSpeedL(-255);
    motorSpeedR(-255);
  }
  // If the left button is pressed on joypad:
  else if(data.equals(LEFT)){
    motorSpeedL(0);
    motorSpeedR(255);
  }
  // If the right button is pressed on joypad:
  else if(data.equals(RIGHT)){
    motorSpeedL(255);
    motorSpeedR(0);
  }
  // If no defined button is pressed on joypad:
  else{
    motorSpeedL(0);
    motorSpeedR(0);
  }
}

// code stored in the sketch: MotorFunctions.ino
// Initializes the left motor's pins:
void motorInitL(){
  // Set all the pins to output, and write LOW to them:
  pinMode(L_EN, OUTPUT);
  digitalWrite(L_EN, LOW);
  pinMode(L_FWD, OUTPUT);
  digitalWrite(L_FWD, LOW);
  pinMode(L_BCK, OUTPUT);
  digitalWrite(L_BCK, LOW);
}

// Initializes the right motor's pins:
void motorInitR(){
  // Set all the pins to output, and write LOW to them:
  pinMode(R_EN, OUTPUT);
  digitalWrite(R_EN, LOW);
  pinMode(R_FWD, OUTPUT);
  digitalWrite(R_FWD, LOW);
  pinMode(R_BCK, OUTPUT);
  digitalWrite(R_BCK, LOW);
}

// Sets the left motor speed from the input. (From -255 to 255)
void motorSpeedL(int spd){
  
  //If the speed is over 0, Set backward low, forward high:
  if(spd > 0){
    digitalWrite(L_BCK, LOW);
    digitalWrite(L_FWD, HIGH);
    analogWrite(L_EN, spd);
  }
  //If the speed is exactly 0, Set everything low:
  else if(spd == 0){
    digitalWrite(L_BCK, LOW);
    digitalWrite(L_FWD, LOW);
    analogWrite(L_EN, spd);
  }
  //If the speed is under 0, Set forward low, backward high:
  else{
    digitalWrite(L_FWD, LOW);
    digitalWrite(L_BCK, HIGH);
    analogWrite(L_EN, -spd);
  }
}

// Sets the right motor speed from the input. (From -255 to 255)
void motorSpeedR(int spd){
  //If the speed is over 0, Set backward low, forward high:
  if(spd > 0){
    digitalWrite(R_BCK, LOW);
    digitalWrite(R_FWD, HIGH);
    analogWrite(R_EN, spd);
  }
  //If the speed is exactly 0, Set everything low:
  else if(spd == 0){
    digitalWrite(R_BCK, LOW);
    digitalWrite(R_FWD, LOW);
    analogWrite(R_EN, spd);
  }
  //If the speed is under 0, Set forward low, backward high:
  else{
    digitalWrite(R_FWD, LOW);
    digitalWrite(R_BCK, HIGH);
    analogWrite(R_EN, -spd);
  }
}
