# Fritzing sketch Eksempel4_Robot_MiniBreadboard_Blueduino (saved by Fritzing 0.9.3b)
breadboards: 1

parts:
  Part1 = Arduino Uno (Rev3)
  IC1 = L293D [package=THT]
  VCC2 = Battery
  VCC3 = Battery
  Part2 = Bluetooth HC-05 Macho
  M1 = DC Motor
  M2 = DC Motor

nets:
  N1: Part1.D8, IC1.In_3
  N2: Part1.D10_PWM/SS, Part2.TXD
  N3: Part1.D11_PWM/MOSI, Part2.RXD
  N4: Part1.D3_PWM, IC1.In_2
  N5: Part1.D4, IC1.In_1
  N6: Part1.D5_PWM, IC1.Enable_1
  N7: Part1.D6_PWM, IC1.Enable_2
  N8: Part1.D7, IC1.In_4
  5V: Part1.5V, IC1.+V, Part2.VCC
  GND: Part1.GND, IC1.0V, VCC3.-, Part2.GND
  N9: IC1.Out_1_(_Controlled_by_Enable_1_), M1.pin_2
  N10: IC1.Out_2_(_Controlled_by_Enable_1_), M1.pin_1
  N11: IC1.+Vmotor, VCC2.+
  N12: IC1.Out_3_(_Controlled_by_Enable_2_), M2.pin_2
  N13: IC1.Out_4_(_Controlled_by_Enable_2_), M2.pin_1
  N14: VCC2.-, VCC3.+

// code stored in the sketch: Eksempel1_Robot_Breadboard.ino
#include <SoftwareSerial.h> // Include the SoftwareSerial library for serial emulation.

// Left motor's Enable, Forward and Back pins: 
#define L_EN 5
#define L_FWD 4
#define L_BCK 3

// Right motor's Enable, Forward and Back pins:
#define R_EN 6
#define R_FWD 7
#define R_BCK 8

// Virtual RX and TX pins for HC-05 communication:
#define V_RX 10
#define V_TX 11

// Define the legal button inputs:
#define UP "b=1"
#define DOWN "b=2"
#define LEFT "b=3"
#define RIGHT "b=4"

SoftwareSerial HC05(V_RX,V_TX); // Virtual serial connection to the HC-05 Module.

String data; // Datastring for the HC-05 messages.

void setup(){
  motorInitL(); // Initialization function for the left motor.
  motorInitR(); // Initialization function for the right motor.
  HC05.begin(115200); // Initiealizes the communication with HC-05 at 115200 baud.
}

void loop(){

  // Check for new messages from HC-05 module:
  if(HC05.available() > 0){
      data = HC05.readStringUntil('#');
  }

  // If the up button is pressed on joypad:
  if(data.equals(UP)){
    motorSpeedL(255);
    motorSpeedR(255);
  }
  // If the down button is pressed on joypad:
  else if(data.equals(DOWN)){
    motorSpeedL(-255);
    motorSpeedR(-255);
  }
  // If the left button is pressed on joypad:
  else if(data.equals(LEFT)){
    motorSpeedL(0);
    motorSpeedR(255);
  }
  // If the right button is pressed on joypad:
  else if(data.equals(RIGHT)){
    motorSpeedL(255);
    motorSpeedR(0);
  }
  // If no defined button is pressed on joypad:
  else{
    motorSpeedL(0);
    motorSpeedR(0);
  }
}

// code stored in the sketch: Eksempel4_Robot_MiniBreadboard_Blueduino.ino
#include <SoftwareSerial.h> // Include the SoftwareSerial library for serial emulation.

// Left motor's Enable, Forward and Back pins: 
#define L_EN 5
#define L_FWD 4
#define L_BCK 3

// Right motor's Enable, Forward and Back pins:
#define R_EN 6
#define R_FWD 7
#define R_BCK 8

// Virtual RX and TX pins for HC-05 communication:
#define V_RX 10
#define V_TX 11

// Define the legal button inputs:
#define UP "b=1"
#define DOWN "b=2"
#define LEFT "b=3"
#define RIGHT "b=4"

// Define the deadzone and threshhold where X and Y are considered unchanged
#define DEADZONE 127
#define THRESHHOLD 50

SoftwareSerial HC05(V_RX,V_TX); // Virtual serial connection to the HC-05 Module.

String data; // Datastring for the HC-05 messages.
char * dataStr; // For turning the data into a classical char array. 
int * dir; // Holds the integer representations of the data.
int x, y = 127; 

void setup(){
  motorInitL(); // Initialization function for the left motor.
  motorInitR(); // Initialization function for the right motor.
  HC05.begin(115200); // Initiealizes the communication with HC-05 at 115200 baud.
}

void loop(){

  // Check for new messages from HC-05 module:
  if(HC05.available() > 0){
      data = HC05.readStringUntil('#');
      dataStr = (char*)data.c_str();
      dir = (int*)strtok(dataStr,"*,");
      x = (uint8_t)dir[0];
      y = (uint8_t)dir[1];
  }

  // If y is 50 bigger than the upper threshhold:
  if(y > DEADZONE+THRESHHOLD){
    motorSpeedL(255);
    motorSpeedR(255);
  }
  // If the down button is pressed on joypad:
  else if(y < DEADZONE-THRESHHOLD){
    motorSpeedL(-255);
    motorSpeedR(-255);
  }
  // If the left button is pressed on joypad:
  else if(x < DEADZONE-THRESHHOLD){
    motorSpeedL(0);
    motorSpeedR(255);
  }
  // If the right button is pressed on joypad:
  else if(x > DEADZONE+THRESHHOLD){
    motorSpeedL(255);
    motorSpeedR(0);
  }
  // If no defined button is pressed on joypad:
  else{
    motorSpeedL(0);
    motorSpeedR(0);
  }
}

// code stored in the sketch: MotorFunctions.ino
// Initializes the left motor's pins:
void motorInitL(){
  // Set all the pins to output, and write LOW to them:
  pinMode(L_EN, OUTPUT);
  digitalWrite(L_EN, LOW);
  pinMode(L_FWD, OUTPUT);
  digitalWrite(L_FWD, LOW);
  pinMode(L_BCK, OUTPUT);
  digitalWrite(L_BCK, LOW);
}

// Initializes the right motor's pins:
void motorInitR(){
  // Set all the pins to output, and write LOW to them:
  pinMode(R_EN, OUTPUT);
  digitalWrite(R_EN, LOW);
  pinMode(R_FWD, OUTPUT);
  digitalWrite(R_FWD, LOW);
  pinMode(R_BCK, OUTPUT);
  digitalWrite(R_BCK, LOW);
}

// Sets the left motor speed from the input. (From -255 to 255)
void motorSpeedL(int spd){
  
  //If the speed is over 0, Set backward low, forward high:
  if(spd > 0){
    digitalWrite(L_BCK, LOW);
    digitalWrite(L_FWD, HIGH);
    analogWrite(L_EN, spd);
  }
  //If the speed is exactly 0, Set everything low:
  else if(spd == 0){
    digitalWrite(L_BCK, LOW);
    digitalWrite(L_FWD, LOW);
    analogWrite(L_EN, spd);
  }
  //If the speed is under 0, Set forward low, backward high:
  else{
    digitalWrite(L_FWD, LOW);
    digitalWrite(L_BCK, HIGH);
    analogWrite(L_EN, -spd);
  }
}

// Sets the right motor speed from the input. (From -255 to 255)
void motorSpeedR(int spd){
  //If the speed is over 0, Set backward low, forward high:
  if(spd > 0){
    digitalWrite(R_BCK, LOW);
    digitalWrite(R_FWD, HIGH);
    analogWrite(R_EN, spd);
  }
  //If the speed is exactly 0, Set everything low:
  else if(spd == 0){
    digitalWrite(R_BCK, LOW);
    digitalWrite(R_FWD, LOW);
    analogWrite(R_EN, spd);
  }
  //If the speed is under 0, Set forward low, backward high:
  else{
    digitalWrite(R_FWD, LOW);
    digitalWrite(R_BCK, HIGH);
    analogWrite(R_EN, -spd);
  }
}
